# Fritzing sketch sequencer (saved by Fritzing 0.9.3b)

parts:
  U1 = NodeMCU V1.0
  U2 = Module 4 Relais 5V [package="Module 4 Relais 5V"]
  R1 = Rotary Potentiometer (Large) [maximum_resistance=100kΩ package=THT]
  S1 = Toggle Switch [package=THT]

nets:
  N1: U1.D3, U2.IN1
  N2: U1.D4, U2.IN2
  3V3: U1.3V3, U2.VCC, R1.leg1, S1.L1
  GND: U1.GND, U2.GND, R1.leg2, S1.L2
  N3: U1.D5, U2.IN3
  N4: U1.D6, U2.IN4
  N5: U1.D7, S1.COM
  N6: U1.A0, R1.wiper
  N7: U2.JD-VCC, U2.VCC2

custom parts:
  NodeMCU V1.0: ESP8266 based NodeMCU
  Module 4 Relais 5V: Module 4 Relais 5V 4x SPD-06VDC-SD-C
